# Fritzing sketch RBTNK-BSP (saved by Fritzing 0.9.3b)
circuit board: 7.65277cm x 13.2267cm
breadboards: 2

parts:
  Arduino_Nano = Arduino Nano (Rev3.0)
  R1 = Resistor [tolerance=±5% resistance=220 package=THT]
  R2 = Resistor [tolerance=±5% resistance=220 package=THT]
  VCC1 = Battery block 9V
  U1_MIDI_In = 3.5mm Audio Jack [package=audio-jack-3.5mm-smd]
  U3 = 3.5mm Audio Jack [package=audio-jack]
  U4 = 3.5mm Audio Jack [package=audio-jack]
  U5 = 3.5mm Audio Jack [package=audio-jack]
  U6 = 3.5mm Audio Jack [package=audio-jack]
  U7 = 3.5mm Audio Jack [package=audio-jack]
  U8 = 3.5mm Audio Jack [package=audio-jack]
  U9 = 3.5mm Audio Jack [package=audio-jack]
  U2 = 3.5mm Audio Jack [package=audio-jack]
  U10 = 3.5mm Audio Jack [package=audio-jack]
  U11 = 3.5mm Audio Jack [package=audio-jack]
  U12 = 3.5mm Audio Jack [package=audio-jack]
  U13 = 3.5mm Audio Jack [package=audio-jack]
  U14 = 3.5mm Audio Jack [package=audio-jack]
  U15 = 3.5mm Audio Jack [package=audio-jack]
  U16 = 3.5mm Audio Jack [package=audio-jack]
  U17 = 3.5mm Audio Jack [package=audio-jack]

nets:
  N1: Arduino_Nano.D0/RX, R1.Pin_1
  N2: Arduino_Nano.GND, VCC1.-, U1_MIDI_In.SLEEVE, U3.SLEEVE, U4.SLEEVE, U5.SLEEVE, U6.SLEEVE, U7.SLEEVE, U8.SLEEVE, U9.SLEEVE, U2.SLEEVE, U10.SLEEVE, U11.SLEEVE, U12.SLEEVE, U13.SLEEVE, U14.SLEEVE, U15.SLEEVE, U16.SLEEVE, U17.SLEEVE
  N3: Arduino_Nano.D2, U8.LEFT
  N4: Arduino_Nano.D3, U7.LEFT
  N5: Arduino_Nano.D4, U9.LEFT
  N6: Arduino_Nano.D5, U6.LEFT
  N7: Arduino_Nano.D6, U5.LEFT
  N8: Arduino_Nano.D9, U4.LEFT
  N9: Arduino_Nano.D10, U3.LEFT
  N10: Arduino_Nano.D11/MOSI, U2.LEFT
  N11: Arduino_Nano.VIN, VCC1.+
  N12: Arduino_Nano.5V, R2.Pin_1
  N13: Arduino_Nano.A7, U14.LEFT
  N14: Arduino_Nano.A6, U12.LEFT
  N15: Arduino_Nano.A5, U10.LEFT
  N16: Arduino_Nano.A4, U13.LEFT
  N17: Arduino_Nano.A3, U11.LEFT
  N18: Arduino_Nano.A2, U16.LEFT
  N19: Arduino_Nano.A1, U17.LEFT
  N20: Arduino_Nano.A0, U15.LEFT
  N21: R1.Pin_0, U1_MIDI_In.RIGHT
  N22: R2.Pin_0, U1_MIDI_In.LEFT
